// Logisim project JOB02_1101.circ as structural Verilog: 4 circuits, main circuit main
module main (
  input  in_1,
  input  in_2,
  input  in_3,
  input  [3:0] in_4,
  input  [3:0] in_5,
  output out_6,
  output out_7,
  output [3:0] out_8,
  output out_9
);

  HA ha_1 (.a(in_1), .b(in_2), .s(out_6), .c(out_7));
  Adder #(.width(4)) adder_1 (.a(in_4), .b(in_5), .out(out_8), .cin(in_3), .cout(out_9));
endmodule

module HA (
  input  a,
  input  b,
  output s,
  output c
);

  and and_1 (c, a, b);
  xor xor_1 (s, a, b);
  LED led_1 (.in(s));
  LED led_2 (.in(c));
endmodule

module FA (
  input  A,
  input  B,
  input  Ci,
  output S,
  output C
);

  wire ha_1_c, ha_1_s, ha_2_c;

  HA ha_1 (.a(A), .b(B), .s(ha_1_s), .c(ha_1_c));
  HA ha_2 (.a(ha_1_s), .b(Ci), .s(S), .c(ha_2_c));
  or or_1 (C, ha_2_c, ha_1_c);
endmodule

module Adder_4bits (
  input  [3:0] A_4,
  input  in_2,
  input  [3:0] B_4,
  output [3:0] S,
  output C
);

  wire fa_1_s, fa_2_s, fa_3_s;

  FA fa_1 (.A(A_4[0]), .B(B_4[0]), .Ci(in_2), .S(fa_1_s), .C(S[0]));
  FA fa_2 (.A(A_4[1]), .B(B_4[1]), .Ci(fa_1_s), .S(fa_2_s), .C(S[1]));
  FA fa_3 (.A(A_4[2]), .B(B_4[2]), .Ci(fa_2_s), .S(fa_3_s), .C(S[2]));
  FA fa_4 (.A(A_4[3]), .B(B_4[3]), .Ci(fa_3_s), .S(C), .C(S[3]));
endmodule
