// Logisim project JOB03_1101.circ as structural Verilog
module HA (
  input  a,
  input  b,
  output s,
  output c
);

  xor xor_1 (s, a, b);
  and and_1 (c, a, b);
endmodule

module FA (
  input  A,
  input  B,
  input  Ci,
  output Sum,
  output Carry
);

  wire ha_1_c, ha_1_s, ha_2_c;

  HA ha_1 (.a(A), .b(B), .s(ha_1_s), .c(ha_1_c));
  HA ha_2 (.a(ha_1_s), .b(Ci), .s(Sum), .c(ha_2_c));
  or or_1 (Carry, ha_2_c, ha_1_c);
endmodule

module HS (
  input  a,
  input  b,
  output d,
  output br
);

  wire not_1_out;

  not not_1 (not_1_out, a);
  xor xor_1 (d, a, b);
  and and_1 (br, not_1_out, b);
endmodule

module FS (
  input  A,
  input  B,
  input  Br0,
  output D,
  output Br
);

  wire hs_1_br, hs_1_d, hs_2_br;

  HS hs_1 (.a(A), .b(B), .d(hs_1_d), .br(hs_1_br));
  HS hs_2 (.a(hs_1_d), .b(Br0), .d(D), .br(hs_2_br));
  or or_1 (Br, hs_2_br, hs_1_br);
endmodule

module sub_4bits (
  input  [3:0] A,
  input  in_2,
  input  [3:0] B,
  output Br,
  output [3:0] D
);

  wire fs_1_br, fs_2_br, fs_3_br;

  FS fs_1 (.A(A[0]), .B(B[0]), .Br0(in_2), .D(D[0]), .Br(fs_1_br));
  FS fs_2 (.A(A[1]), .B(B[1]), .Br0(fs_1_br), .D(D[1]), .Br(fs_2_br));
  FS fs_3 (.A(A[2]), .B(B[2]), .Br0(fs_2_br), .D(D[2]), .Br(fs_3_br));
  FS fs_4 (.A(A[3]), .B(B[3]), .Br0(fs_3_br), .D(D[3]), .Br(Br));
endmodule

module p_add_sub_4bits (
  input  [3:0] A,
  input  in_2,
  input  [3:0] B,
  output Br,
  output [3:0] D
);

  wire fa_1_carry, fa_2_carry, fa_3_carry;

  FA fa_1 (.A(A[0]), .B(B[0]), .Ci(in_2), .Sum(D[0]), .Carry(fa_1_carry));
  FA fa_2 (.A(A[1]), .B(B[1]), .Ci(fa_1_carry), .Sum(D[1]), .Carry(fa_2_carry));
  FA fa_3 (.A(A[2]), .B(B[2]), .Ci(fa_2_carry), .Sum(D[2]), .Carry(fa_3_carry));
  FA fa_4 (.A(A[3]), .B(B[3]), .Ci(fa_3_carry), .Sum(D[3]), .Carry(Br));
endmodule
