// Logisim project JOB04_1101.circ as structural Verilog
module HA (
  input  a,
  input  b,
  output s,
  output c
);

  xor xor_1 (s, a, b);
  and and_1 (c, a, b);
endmodule

module FA (
  input  A,
  input  B,
  input  Ci,
  output Sum,
  output Carry
);

  wire ha_1_c, ha_1_s, ha_2_c;

  HA ha_1 (.a(A), .b(B), .s(ha_1_s), .c(ha_1_c));
  HA ha_2 (.a(ha_1_s), .b(Ci), .s(Sum), .c(ha_2_c));
  or or_1 (Carry, ha_2_c, ha_1_c);
endmodule

module HS (
  input  a,
  input  b,
  output d,
  output br
);

  wire not_1_out;

  not not_1 (not_1_out, a);
  xor xor_1 (d, a, b);
  and and_1 (br, not_1_out, b);
endmodule

module FS (
  input  A,
  input  B,
  input  Br0,
  output D,
  output Br
);

  wire hs_1_br, hs_1_d, hs_2_br;

  HS hs_1 (.a(A), .b(B), .d(hs_1_d), .br(hs_1_br));
  HS hs_2 (.a(hs_1_d), .b(Br0), .d(D), .br(hs_2_br));
  or or_1 (Br, hs_2_br, hs_1_br);
endmodule

module sub_4bits (
  input  [3:0] A,
  input  in_2,
  input  [3:0] B,
  output Br,
  output [3:0] D
);

  wire fs_1_br, fs_2_br, fs_3_br;

  FS fs_1 (.A(A[0]), .B(B[0]), .Br0(in_2), .D(D[0]), .Br(fs_1_br));
  FS fs_2 (.A(A[1]), .B(B[1]), .Br0(fs_1_br), .D(D[1]), .Br(fs_2_br));
  FS fs_3 (.A(A[2]), .B(B[2]), .Br0(fs_2_br), .D(D[2]), .Br(fs_3_br));
  FS fs_4 (.A(A[3]), .B(B[3]), .Br0(fs_3_br), .D(D[3]), .Br(Br));
endmodule

module p_add_sub_4bits (
  input  [3:0] A,
  input  sel,
  input  [3:0] B,
  output C,
  output [3:0] Sum
);

  wire fa_1_carry, fa_2_carry, fa_3_carry, xor_1_out, xor_2_out, xor_3_out, xor_4_out;

  xor xor_1 (xor_1_out, sel, B[0]);
  FA fa_1 (.A(A[0]), .B(xor_1_out), .Ci(sel), .Sum(Sum[0]), .Carry(fa_1_carry));
  xor xor_2 (xor_2_out, sel, B[1]);
  FA fa_2 (.A(A[1]), .B(xor_2_out), .Ci(fa_1_carry), .Sum(Sum[1]), .Carry(fa_2_carry));
  xor xor_3 (xor_3_out, sel, B[2]);
  FA fa_3 (.A(A[2]), .B(xor_3_out), .Ci(fa_2_carry), .Sum(Sum[2]), .Carry(fa_3_carry));
  xor xor_4 (xor_4_out, sel, B[3]);
  FA fa_4 (.A(A[3]), .B(xor_4_out), .Ci(fa_3_carry), .Sum(Sum[3]), .Carry(C));
endmodule

module comp (
  input  A,
  input  B,
  output Y_eq,
  output Y_neq,
  output Y_a_b,
  output Y_b_a
);

  wire not_1_out, not_2_out;

  not not_1 (not_1_out, B);
  not not_2 (not_2_out, A);
  xnor xnor_1 (Y_eq, A, B);
  xor xor_1 (Y_neq, A, B);
  and and_1 (Y_a_b, A, not_1_out);
  and and_2 (Y_b_a, not_2_out, B);
endmodule

module encoder (
  input  D7,
  input  D6,
  input  D5,
  input  D4,
  input  D3,
  input  D2,
  input  D1,
  input  D0,
  output Y2_C,
  output Y2_B,
  output Y2_A
);

  or or_1 (Y2_C, D4, D5, D6, D7);
  or or_2 (Y2_B, D2, D3, D6, D7);
  or or_3 (Y2_A, D1, D3, D5, D7);
endmodule

module decode (
  input  C_2,
  input  B_1,
  input  A_0,
  output D7,
  output D6,
  output D5,
  output D4,
  output D3,
  output D2,
  output D1,
  output D0
);

  wire not_1_out, not_2_out, not_3_out;

  not not_1 (not_1_out, C_2);
  not not_2 (not_2_out, B_1);
  not not_3 (not_3_out, A_0);
  and and_1 (D7, C_2, B_1, A_0);
  and and_2 (D6, C_2, B_1, not_3_out);
  and and_3 (D5, C_2, not_2_out, A_0);
  and and_4 (D4, C_2, not_2_out, not_3_out);
  and and_5 (D3, not_1_out, B_1, A_0);
  and and_6 (D2, not_1_out, B_1, not_3_out);
  and and_7 (D1, not_1_out, not_2_out, A_0);
  and and_8 (D0, not_1_out, not_2_out, not_3_out);
endmodule

module Mux (
  input  In0,
  input  In1,
  input  In2,
  input  In3,
  input  in_5,
  input  in_6,
  output Y_out
);

  wire and_1_out, and_2_out, and_3_out, and_4_out, not_1_out, not_2_out;

  not not_1 (not_1_out, in_5);
  and and_1 (and_1_out, In0, not_1_out, not_2_out);
  and and_2 (and_2_out, In1, not_1_out, in_6);
  and and_3 (and_3_out, In2, in_5, not_2_out);
  and and_4 (and_4_out, In3, in_5, in_6);
  not not_2 (not_2_out, in_6);
  or or_1 (Y_out, and_1_out, and_2_out, and_3_out, and_4_out);
endmodule
