// Logisim project JOB05_1101.circ as structural Verilog
module DeMux (
  input  indata,
  input  s1,
  input  s0,
  output out0,
  output out1,
  output out2,
  output out3
);

  wire not_1_out, not_2_out;

  not not_1 (not_1_out, s1);
  not not_2 (not_2_out, s0);
  and and_1 (out0, indata, not_1_out, not_2_out);
  and and_2 (out1, indata, not_1_out, s0);
  and and_3 (out2, indata, s1, not_2_out);
  and and_4 (out3, indata, s1, s0);
endmodule

module latch (
  input  R,
  input  s,
  output Q,
  output Qbar
);

  xor xor_1 (Q, R, Qbar);
  xor xor_2 (Qbar, Q, s);
endmodule

module RSFF (
  input  R,
  input  CLK,
  input  s,
  output Q,
  output Qbar
);

  wire and_1_out, and_2_out;

  and and_1 (and_1_out, R, CLK);
  and and_2 (and_2_out, CLK, s);
  xor xor_1 (Q, and_1_out, Qbar);
  xor xor_2 (Qbar, Q, and_2_out);
endmodule

module JKFF (
  input  K,
  input  CLK,
  input  J,
  output Q,
  output Qbar
);

  wire and_1_out, and_2_out;

  and and_1 (and_1_out, K, Q, CLK);
  and and_2 (and_2_out, CLK, Qbar, J);
  xor xor_1 (Q, and_1_out, Qbar);
  xor xor_2 (Qbar, Q, and_2_out);
endmodule

module DFF (
  input  CLK,
  input  D,
  output Q,
  output Qbar
);

  wire and_1_out, and_2_out, not_1_out;

  not not_1 (not_1_out, D);
  and and_1 (and_1_out, not_1_out, Q, CLK);
  and and_2 (and_2_out, CLK, Qbar, D);
  xor xor_1 (Q, and_1_out, Qbar);
  xor xor_2 (Qbar, Q, and_2_out);
endmodule

module TFF (
  input  CLK,
  input  D,
  output Q,
  output Qbar
);

  wire and_1_out, and_2_out;

  and and_1 (and_1_out, D, Q, CLK);
  and and_2 (and_2_out, CLK, Qbar, D);
  xor xor_1 (Q, and_1_out, Qbar);
  xor xor_2 (Qbar, Q, and_2_out);
endmodule

module test (
  input  in_1,
  input  in_2,
  input  in_3,
  input  in_4,
  input  in_5,
  input  in_6,
  input  in_7,
  input  in_8,
  input  in_9,
  input  in_10,
  input  in_11,
  input  in_12,
  input  in_13,
  input  in_14,
  output out_15,
  output out_16,
  output out_17,
  output out_18,
  output out_19,
  output out_20
);

  wire not_1_out, not_2_out;

  S_R_Flip_Flop #(.trigger("low")) s_r_ff_1 (.S(in_1), .R(in_3), .clk(in_5), .Q(out_15));  // open: reset, Qn, preset
  J_K_Flip_Flop j_k_ff_1 (.J(in_7), .K(not_1_out), .clk(in_11), .Q(out_17));  // open: Qn, preset, reset
  not not_1 (not_1_out, in_7);
  D_Flip_Flop d_ff_1 (.D(in_8), .clk(in_12), .Q(out_18));  // open: Qn, preset, reset
  J_K_Flip_Flop j_k_ff_2 (.J(in_2), .K(in_4), .clk(in_6), .Q(out_16));  // open: Qn, preset, reset
  J_K_Flip_Flop j_k_ff_3 (.J(in_9), .K(not_2_out), .clk(in_13), .Q(out_19));  // open: Qn, preset, reset
  not not_2 (not_2_out, in_9);
  T_Flip_Flop t_ff_1 (.T(in_10), .clk(in_14), .Q(out_20));  // open: Qn, reset, preset
endmodule

module siso (
  input  in_1,
  output out_2
);

  wire clock_1_out, d_ff_1_q, d_ff_2_q, d_ff_3_q;

  Clock clock_1 (.out(clock_1_out));
  D_Flip_Flop d_ff_1 (.D(in_1), .clk(clock_1_out), .Q(d_ff_1_q));  // open: Qn, preset, reset
  D_Flip_Flop d_ff_2 (.D(d_ff_1_q), .clk(clock_1_out), .Q(d_ff_2_q));  // open: Qn, preset, reset
  D_Flip_Flop d_ff_3 (.D(d_ff_2_q), .clk(clock_1_out), .Q(d_ff_3_q));  // open: Qn, preset, reset
  D_Flip_Flop d_ff_4 (.D(d_ff_3_q), .clk(clock_1_out), .Q(out_2));  // open: Qn, preset, reset
endmodule
