// Logisim project JOB06_1101.circ as structural Verilog
module siso (
  input  ind,
  output outd
);

  wire CLK_out, d_ff_1_q, d_ff_2_q, d_ff_3_q;

  Clock CLK (.out(CLK_out));
  D_Flip_Flop d_ff_1 (.D(ind), .clk(CLK_out), .Q(d_ff_1_q));  // open: Qn, preset, reset
  D_Flip_Flop d_ff_2 (.D(d_ff_1_q), .clk(CLK_out), .Q(d_ff_2_q));  // open: Qn, preset, reset
  D_Flip_Flop d_ff_3 (.D(d_ff_2_q), .clk(CLK_out), .Q(d_ff_3_q));  // open: Qn, preset, reset
  D_Flip_Flop d_ff_4 (.D(d_ff_3_q), .clk(CLK_out), .Q(outd));  // open: Qn, preset, reset
endmodule

module sipo (
  input  ind,
  output out0,
  output out1,
  output out2,
  output out3
);

  wire CLK_out;

  Clock CLK (.out(CLK_out));
  D_Flip_Flop d_ff_1 (.D(ind), .clk(CLK_out), .Q(out0));  // open: Qn, preset, reset
  D_Flip_Flop d_ff_2 (.D(out0), .clk(CLK_out), .Q(out1));  // open: Qn, preset, reset
  D_Flip_Flop d_ff_3 (.D(out1), .clk(CLK_out), .Q(out2));  // open: Qn, preset, reset
  D_Flip_Flop d_ff_4 (.D(out2), .clk(CLK_out), .Q(out3));  // open: Qn, preset, reset
endmodule

module piso (
  input  SH_LDbar,
  input  in0,
  input  in1,
  input  in2,
  input  in3,
  output outd
);

  wire and_1_out, and_2_out, and_3_out, and_4_out, and_5_out, and_6_out, CLK_out, d_ff_1_q, d_ff_2_q,
       d_ff_3_q, not_1_out, or_1_out, or_2_out, or_3_out;

  not not_1 (not_1_out, SH_LDbar);
  Clock CLK (.out(CLK_out));
  D_Flip_Flop d_ff_1 (.D(in0), .clk(CLK_out), .Q(d_ff_1_q));  // open: Qn, preset, reset
  and and_1 (and_1_out, d_ff_1_q, SH_LDbar);
  and and_2 (and_2_out, not_1_out, in1);
  or or_1 (or_1_out, and_1_out, and_2_out);
  D_Flip_Flop d_ff_2 (.D(or_1_out), .clk(CLK_out), .Q(d_ff_2_q));  // open: Qn, preset, reset
  and and_3 (and_3_out, d_ff_2_q, SH_LDbar);
  and and_4 (and_4_out, not_1_out, in2);
  or or_2 (or_2_out, and_3_out, and_4_out);
  D_Flip_Flop d_ff_3 (.D(or_2_out), .clk(CLK_out), .Q(d_ff_3_q));  // open: Qn, preset, reset
  and and_5 (and_5_out, d_ff_3_q, SH_LDbar);
  and and_6 (and_6_out, not_1_out, in3);
  or or_3 (or_3_out, and_5_out, and_6_out);
  D_Flip_Flop d_ff_4 (.D(or_3_out), .clk(CLK_out), .Q(outd));  // open: Qn, preset, reset
endmodule

module pipo (
  input  in0,
  input  in1,
  input  in2,
  input  in3,
  output out0,
  output out1,
  output out2,
  output out3
);

  wire CLK_out;

  Clock CLK (.out(CLK_out));
  D_Flip_Flop d_ff_1 (.D(in0), .clk(CLK_out), .Q(out0));  // open: Qn, preset, reset
  D_Flip_Flop d_ff_2 (.D(in1), .clk(CLK_out), .Q(out1));  // open: Qn, preset, reset
  D_Flip_Flop d_ff_3 (.D(in2), .clk(CLK_out), .Q(out2));  // open: Qn, preset, reset
  D_Flip_Flop d_ff_4 (.D(in3), .clk(CLK_out), .Q(out3));  // open: Qn, preset, reset
endmodule

module recirc (
  input  control,
  input  ind,
  output outd
);

  wire and_1_out, and_2_out, CLK_out, d_ff_1_q, d_ff_2_q, d_ff_3_q, not_1_out, or_1_out;

  not not_1 (not_1_out, control);
  and and_1 (and_1_out, outd, not_1_out);
  and and_2 (and_2_out, control, ind);
  Clock CLK (.out(CLK_out));
  or or_1 (or_1_out, and_1_out, and_2_out);
  D_Flip_Flop d_ff_1 (.D(or_1_out), .clk(CLK_out), .Q(d_ff_1_q));  // open: Qn, preset, reset
  D_Flip_Flop d_ff_2 (.D(d_ff_1_q), .clk(CLK_out), .Q(d_ff_2_q));  // open: Qn, preset, reset
  D_Flip_Flop d_ff_3 (.D(d_ff_2_q), .clk(CLK_out), .Q(d_ff_3_q));  // open: Qn, preset, reset
  D_Flip_Flop d_ff_4 (.D(d_ff_3_q), .clk(CLK_out), .Q(outd));  // open: Qn, preset, reset

  // Notes on the sheet:
  //   1_high : 직렬 데이터 입력
  //   0_low : 재순환 데이터 입력
endmodule

module dual_shift (
  input  ind,
  output out0,
  output out1,
  output out2,
  output out3
);

  wire CLK_out;

  Clock CLK (.out(CLK_out));
  D_Flip_Flop d_ff_1 (.clk(CLK_out));  // open: D, Q, Qn, preset, reset
  D_Flip_Flop d_ff_2 (.clk(CLK_out));  // open: D, Q, Qn, preset, reset
  D_Flip_Flop d_ff_3 (.clk(CLK_out));  // open: D, Q, Qn, preset, reset
  D_Flip_Flop d_ff_4 (.clk(CLK_out));  // open: D, Q, Qn, preset, reset
endmodule

module MUX_2 (
  input  SLI,
  input  SRI,
  input  R_Lbar,
  output Y
);

  wire and_1_out, and_2_out, not_1_out;

  not not_1 (not_1_out, R_Lbar);
  and and_1 (and_1_out, SLI, not_1_out);
  and and_2 (and_2_out, R_Lbar, SRI);
  or or_1 (Y, and_1_out, and_2_out);
endmodule
